# Fritzing sketch Incubator-Fritzing (saved by Fritzing 0.9.3b)
breadboards: 2

parts:
  80mm_Fan = DC Motor
  MOSFET1 = Basic FET N-Channel [package="TO220 [THT]"]
  Pushbutton_1 = Pushbutton [package="[THT]"]
  Pushbutton_2 = Pushbutton [package="[THT]"]
  R6_-_Pull_down_for_MOSFET_1 = Resistor [tolerance=±5% resistance=10k package=THT]
  Diode1 = Rectifier Diode [part_number=1N4001 package="300 mil [THT]"]
  Power_plug1 = Power plug
  R8_-_Pull_up_for_Temp1 = Resistor [tolerance=±5% resistance=10k package=THT]
  R9_-_Pull_down_for_button_1 = Resistor [tolerance=±5% resistance=10k package=THT]
  Arduino1 = Arduino Uno (Rev3)
  LCD2 = LCD screen  # not connected
  U2 = mystery part, 4 pins [chip_label=I2C spacing=300mil]
  MOSFET2 = Basic FET N-Channel [package="TO220 [THT]"]
  R6_-_Pull_down_for_MOSFET_2 = Resistor [tolerance=±5% resistance=10k package=THT]
  R2 = Resistor [tolerance=±5% resistance=1.5 power=22W package=THT]
  R10_-_Pull_down_for_button_2 = Resistor [tolerance=±5% resistance=10k package=THT]
  R1 = Temperature Sensor (Thermistor) [thermistor_type=NTC package=THT]

nets (from the schematic view):
  VCC: 80mm_Fan.pin_1, Diode1.cathode, Power_plug1.VCC, Arduino1.VIN, R2.Pin_0
  N1: 80mm_Fan.pin_2, MOSFET1.drain, Diode1.anode
  N2: MOSFET1.gate, R6_-_Pull_down_for_MOSFET_1.Pin_1, Arduino1.D5_PWM
  GND: MOSFET1.source, R6_-_Pull_down_for_MOSFET_1.Pin_0, Power_plug1.GND, Arduino1.GND, U2.pin4, MOSFET2.source, R6_-_Pull_down_for_MOSFET_2.Pin_0
  N3: Pushbutton_1.Pin_1, Pushbutton_1.Pin_2, R9_-_Pull_down_for_button_1.Pin_1, Arduino1.D11_PWM/MOSI
  N4: Pushbutton_1.Pin_3, Pushbutton_1.Pin_4, Pushbutton_2.Pin_3, Pushbutton_2.Pin_4, R8_-_Pull_up_for_Temp1.Pin_0, Arduino1.5V, U2.pin3
  N5: Pushbutton_2.Pin_1, Pushbutton_2.Pin_2, Arduino1.D12/MISO, R10_-_Pull_down_for_button_2.Pin_0
  N6: R8_-_Pull_up_for_Temp1.Pin_1, Arduino1.A0
  N7: R9_-_Pull_down_for_button_1.Pin_0, R10_-_Pull_down_for_button_2.Pin_1, R1.pin_0
  N8: Arduino1.A4/SDA, U2.pin2
  N9: Arduino1.A5/SCL, U2.pin1
  N10: Arduino1.D6_PWM, MOSFET2.gate, R6_-_Pull_down_for_MOSFET_2.Pin_1
  N11: MOSFET2.drain, R2.Pin_1

notes:
  Fan
  Temp Sensor
  User interface buttons
  Push buttons
  Fan conroller
  12V power supply
  LCD I2C interface
  SCL - A5
  SDA - A4
  Vcc
  Gnd
  Heating Pad
  LCD I2C controller
  12V input
